// Logisim project miniMIPS.circ as structural Verilog: 7 circuits, main circuit main
module main (
  input  Reset
);

  wire alu_32_bits_1_zero, and_1_out, clock_1_out, clock_2_out, clock_3_out, control_1_alusrc,
       control_1_branch, control_1_memtoreg, control_1_memwrite, control_1_regwrite, not_1_out;
  wire [3:0] control_1_alucontrol;
  wire [7:0] memoryconverter_1_out_2, memoryconverter_2_out_2;
  wire [31:0] adder_1_out, adder_2_out, alu_32_bits_1_q, bit_extender_1_out, multiplexer_1_out,
       multiplexer_2_out, multiplexer_3_out, pc_1_pc_out, ram_1_dout, register_file_1_readdata1,
       register_file_1_readdata2, rom_1_data, shifter_1_out;

  Multiplexer #(.width(32)) multiplexer_1 (
    .in0(adder_1_out), .in1(adder_2_out), .out(multiplexer_1_out), .sel(and_1_out));
  Clock clock_1 (.out(clock_1_out));
  PC pc_1 (.PC_in(multiplexer_1_out), .Clock(clock_1_out), .Reset(Reset), .PC_out(pc_1_pc_out));
  ROM #(.dataWidth(32)) rom_1 (.addr(memoryconverter_1_out_2), .data(rom_1_data));
  MemoryConverter memoryconverter_1 (.in_1(pc_1_pc_out), .out_2(memoryconverter_1_out_2));
  Adder #(.width(32)) adder_1 (.a(32'h4), .b(pc_1_pc_out), .out(adder_1_out));  // open: cin, cout
  Clock clock_2 (.out(clock_2_out));
  assign bit_extender_1_out = {{16{rom_1_data[15]}}, rom_1_data[15:0]};  // Bit_Extender bit_extender_1
  control control_1 (
    .opcode(rom_1_data[31:26]), .MemWrite(control_1_memwrite), .MemToReg(control_1_memtoreg),
    .Branch(control_1_branch), .ALUSrc(control_1_alusrc), .RegWrite(control_1_regwrite),
    .ALUControl(control_1_alucontrol));
  register_file register_file_1 (
    .Clock(clock_2_out), .Reset(Reset), .ReadReg1(rom_1_data[25:21]), .ReadReg2(rom_1_data[20:16]),
    .WriteReg(rom_1_data[20:16]), .WriteData(multiplexer_3_out), .WriteEnable(control_1_regwrite),
    .ReadData1(register_file_1_readdata1), .ReadData2(register_file_1_readdata2));
  Multiplexer #(.width(32)) multiplexer_2 (
    .in0(register_file_1_readdata2), .in1(bit_extender_1_out), .out(multiplexer_2_out), .sel(control_1_alusrc));
  Shifter #(.width(32)) shifter_1 (.in(bit_extender_1_out), .\dist (5'b00010), .out(shifter_1_out));
  ALU_32_bits alu_32_bits_1 (
    .A(register_file_1_readdata1), .B(multiplexer_2_out), .Operation(control_1_alucontrol),
    .Q(alu_32_bits_1_q), .zero(alu_32_bits_1_zero));  // open: carry_out
  Adder #(.width(32)) adder_2 (.a(shifter_1_out), .b(adder_1_out), .out(adder_2_out));  // open: cin, cout
  and and_1 (and_1_out, control_1_branch, not_1_out);
  not not_1 (not_1_out, alu_32_bits_1_zero);
  Clock clock_3 (.out(clock_3_out));
  RAM #(.asyncread("true"), .clearpin("true"), .dataWidth(32)) ram_1 (
    .addr(memoryconverter_2_out_2), .we(control_1_memwrite), .clk(clock_3_out),
    .din(register_file_1_readdata2), .dout(ram_1_dout), .clr(Reset));  // open: oe
  MemoryConverter memoryconverter_2 (.in_1(alu_32_bits_1_q), .out_2(memoryconverter_2_out_2));
  Multiplexer #(.width(32)) multiplexer_3 (
    .in0(alu_32_bits_1_q), .in1(ram_1_dout), .out(multiplexer_3_out), .sel(control_1_memtoreg));

  // Notes on the sheet:
  //   PC
  //   Address
  //   contents of rom_1 (hex, n*v repeats v):
  //   20080005 ac080000 8c090000 21080001 15090001 200a000a 200b000f ac080000
  //   (Only supports addresses 0x00400000 to 0x0040000ff)
  //   Ignore addresses on the side
  //   (To get the address from the number on the side do 0x00400000+number*4)
  //   Instruction memory
  //   Inst
  //   OP
  //   RS
  //   RT
  //   IMM
  //   Register file
  //   rt or imm
  //   >>2
  //   WriteData in rt to memory
  //   ShiftImm2
  //   PC+4
  //   PCBranch
  //   Address
  //   WriteEnable
  //   Clear
  //   Clock
  //   (Only supports addresses 0x10010000 to 0x100100ff)
  //   Ignore addresses on the side
  //   (To get the address from the number on the side do 0x10010000+number*4)
  //   Data memory
  //   ReadData
  //   Writeback
endmodule

module control (
  input  [5:0] opcode,
  output MemWrite,
  output MemToReg,
  output Branch,
  output ALUSrc,
  output RegWrite,
  output [3:0] ALUControl
);

  wire and_2_out, not_1_out, not_2_out, not_3_out, not_4_out, not_5_out, not_6_out, or_2_out;
  wire [3:0] controlled_buffer_1_out, controlled_buffer_2_out;

  not not_1 (not_1_out, opcode[5]);
  not not_2 (not_2_out, opcode[4]);
  not not_3 (not_3_out, opcode[3]);
  not not_4 (not_4_out, opcode[2]);
  not not_5 (not_5_out, opcode[1]);
  not not_6 (not_6_out, opcode[0]);
  // AND_Gate and_1 has open pins: in0=not_1_out, in1=not_2_out, in2=not_3_out, in3=not_4_out, in4=not_5_out, in5=not_6_out, out=open
  and and_2 (and_2_out, not_1_out, not_2_out, opcode[3], not_4_out, not_5_out, not_6_out);
  and and_3 (MemToReg, opcode[5], not_2_out, not_3_out, not_4_out, opcode[1], opcode[0]);
  and and_4 (MemWrite, opcode[5], not_2_out, opcode[3], not_4_out, opcode[1], opcode[0]);
  and and_5 (Branch, not_1_out, not_2_out, not_3_out, opcode[2], not_5_out, opcode[0]);
  or or_1 (RegWrite, and_2_out, MemToReg);
  or or_2 (or_2_out, and_2_out, MemToReg, MemWrite);
  assign controlled_buffer_1_out = or_2_out ? 4'b0010 : 4'bz;  // Controlled_Buffer controlled_buffer_1
  assign controlled_buffer_2_out = Branch ? 4'b0110 : 4'bz;  // Controlled_Buffer controlled_buffer_2
  Multiplexer #(.width(4)) multiplexer_1 (
    .in0(controlled_buffer_1_out), .in1(controlled_buffer_2_out), .out(ALUControl), .sel(Branch));
  or or_3 (ALUSrc, MemWrite, MemToReg, and_2_out);

  // Notes on the sheet:
  //   o0
  //   bne
  //   R Type 000000
  //   Addi 001000
  //   lw 100011
  //   sw 101011
  //   add 0010
  //   sub 0110
endmodule

module register_file (
  input  WriteEnable,
  input  Clock,
  input  Reset,
  input  [4:0] ReadReg1,
  input  [4:0] ReadReg2,
  input  [4:0] WriteReg,
  input  [31:0] WriteData,
  output [31:0] ReadData1,
  output [31:0] ReadData2
);

  wire and_1_out, and_2_out, and_3_out, and_4_out, and_5_out, and_6_out, and_7_out, and_8_out, and_9_out,
       and_10_out, and_11_out, and_12_out, and_13_out, and_14_out, and_15_out, and_16_out, and_17_out,
       and_18_out, and_19_out, and_20_out, and_21_out, and_22_out, and_23_out, and_24_out, and_25_out,
       and_26_out, and_27_out, and_28_out, and_29_out, and_30_out, and_31_out, and_32_out, decoder_1_out0,
       decoder_1_out1, decoder_1_out2, decoder_1_out3, decoder_1_out4, decoder_1_out5, decoder_1_out6,
       decoder_1_out7, decoder_1_out8, decoder_1_out9, decoder_1_out10, decoder_1_out11, decoder_1_out12,
       decoder_1_out13, decoder_1_out14, decoder_1_out15, decoder_1_out16, decoder_1_out17, decoder_1_out18,
       decoder_1_out19, decoder_1_out20, decoder_1_out21, decoder_1_out22, decoder_1_out23, decoder_1_out24,
       decoder_1_out25, decoder_1_out26, decoder_1_out27, decoder_1_out28, decoder_1_out29, decoder_1_out30,
       decoder_1_out31;
  wire [31:0] register_1_q, register_2_q, register_3_q, register_4_q, register_5_q, register_6_q,
       register_7_q, register_8_q, register_9_q, register_10_q, register_11_q, register_12_q, register_13_q,
       register_14_q, register_15_q, register_16_q, register_17_q, register_18_q, register_19_q,
       register_20_q, register_21_q, register_22_q, register_23_q, register_24_q, register_25_q,
       register_26_q, register_27_q, register_28_q, register_29_q, register_30_q, register_31_q,
       register_32_q;

  Decoder #(.select(5)) decoder_1 (
    .out0(decoder_1_out0), .out1(decoder_1_out1), .out2(decoder_1_out2), .out3(decoder_1_out3),
    .out4(decoder_1_out4), .out5(decoder_1_out5), .out6(decoder_1_out6), .out7(decoder_1_out7),
    .out8(decoder_1_out8), .out9(decoder_1_out9), .out10(decoder_1_out10), .out11(decoder_1_out11),
    .out12(decoder_1_out12), .out13(decoder_1_out13), .out14(decoder_1_out14), .out15(decoder_1_out15),
    .out16(decoder_1_out16), .out17(decoder_1_out17), .out18(decoder_1_out18), .out19(decoder_1_out19),
    .out20(decoder_1_out20), .out21(decoder_1_out21), .out22(decoder_1_out22), .out23(decoder_1_out23),
    .out24(decoder_1_out24), .out25(decoder_1_out25), .out26(decoder_1_out26), .out27(decoder_1_out27),
    .out28(decoder_1_out28), .out29(decoder_1_out29), .out30(decoder_1_out30), .out31(decoder_1_out31),
    .sel(WriteReg));  // open: en
  and and_1 (and_1_out, decoder_1_out0, WriteEnable);
  and and_2 (and_2_out, decoder_1_out1, WriteEnable);
  and and_3 (and_3_out, decoder_1_out2, WriteEnable);
  and and_4 (and_4_out, decoder_1_out3, WriteEnable);
  and and_5 (and_5_out, decoder_1_out4, WriteEnable);
  and and_6 (and_6_out, decoder_1_out5, WriteEnable);
  and and_7 (and_7_out, decoder_1_out6, WriteEnable);
  and and_8 (and_8_out, decoder_1_out7, WriteEnable);
  and and_9 (and_9_out, decoder_1_out8, WriteEnable);
  and and_10 (and_10_out, decoder_1_out9, WriteEnable);
  and and_11 (and_11_out, decoder_1_out10, WriteEnable);
  and and_12 (and_12_out, decoder_1_out11, WriteEnable);
  and and_13 (and_13_out, decoder_1_out12, WriteEnable);
  and and_14 (and_14_out, decoder_1_out13, WriteEnable);
  and and_15 (and_15_out, decoder_1_out14, WriteEnable);
  and and_16 (and_16_out, decoder_1_out15, WriteEnable);
  and and_17 (and_17_out, decoder_1_out16, WriteEnable);
  and and_18 (and_18_out, decoder_1_out17, WriteEnable);
  and and_19 (and_19_out, decoder_1_out18, WriteEnable);
  and and_20 (and_20_out, decoder_1_out19, WriteEnable);
  and and_21 (and_21_out, decoder_1_out20, WriteEnable);
  and and_22 (and_22_out, decoder_1_out21, WriteEnable);
  and and_23 (and_23_out, decoder_1_out22, WriteEnable);
  and and_24 (and_24_out, decoder_1_out23, WriteEnable);
  and and_25 (and_25_out, decoder_1_out24, WriteEnable);
  and and_26 (and_26_out, decoder_1_out25, WriteEnable);
  and and_27 (and_27_out, decoder_1_out26, WriteEnable);
  and and_28 (and_28_out, decoder_1_out27, WriteEnable);
  and and_29 (and_29_out, decoder_1_out28, WriteEnable);
  and and_30 (and_30_out, decoder_1_out29, WriteEnable);
  and and_31 (and_31_out, decoder_1_out30, WriteEnable);
  and and_32 (and_32_out, decoder_1_out31, WriteEnable);
  Register #(.trigger("high"), .width(32)) register_1 (
    .D({32{1'b0}}), .en(1'b1), .clk(1'b1), .Q(register_1_q));  // open: clr
  Register #(.trigger("high"), .width(32)) register_2 (
    .D(32'h10010000), .en(1'b1), .clk(1'b1), .Q(register_2_q));  // open: clr
  Register #(.width(32)) register_3 (.D(WriteData), .en(and_3_out), .clk(Clock), .Q(register_3_q), .clr(Reset));
  Register #(.width(32)) register_4 (.D(WriteData), .en(and_4_out), .clk(Clock), .Q(register_4_q), .clr(Reset));
  Register #(.width(32)) register_5 (.D(WriteData), .en(and_5_out), .clk(Clock), .Q(register_5_q), .clr(Reset));
  Register #(.width(32)) register_6 (.D(WriteData), .en(and_6_out), .clk(Clock), .Q(register_6_q), .clr(Reset));
  Register #(.width(32)) register_7 (.D(WriteData), .en(and_7_out), .clk(Clock), .Q(register_7_q), .clr(Reset));
  Register #(.width(32)) register_8 (.D(WriteData), .en(and_8_out), .clk(Clock), .Q(register_8_q), .clr(Reset));
  Register #(.width(32)) register_9 (.D(WriteData), .en(and_9_out), .clk(Clock), .Q(register_9_q), .clr(Reset));
  Register #(.width(32)) register_10 (.D(WriteData), .en(and_10_out), .clk(Clock), .Q(register_10_q), .clr(Reset));
  Register #(.width(32)) register_11 (.D(WriteData), .en(and_11_out), .clk(Clock), .Q(register_11_q), .clr(Reset));
  Register #(.width(32)) register_12 (.D(WriteData), .en(and_12_out), .clk(Clock), .Q(register_12_q), .clr(Reset));
  Register #(.width(32)) register_13 (.D(WriteData), .en(and_13_out), .clk(Clock), .Q(register_13_q), .clr(Reset));
  Register #(.width(32)) register_14 (.D(WriteData), .en(and_14_out), .clk(Clock), .Q(register_14_q), .clr(Reset));
  Register #(.width(32)) register_15 (.D(WriteData), .en(and_15_out), .clk(Clock), .Q(register_15_q), .clr(Reset));
  Register #(.width(32)) register_16 (.D(WriteData), .en(and_16_out), .clk(Clock), .Q(register_16_q), .clr(Reset));
  Register #(.width(32)) register_17 (.D(WriteData), .en(and_17_out), .clk(Clock), .Q(register_17_q), .clr(Reset));
  Register #(.width(32)) register_18 (.D(WriteData), .en(and_18_out), .clk(Clock), .Q(register_18_q), .clr(Reset));
  Register #(.width(32)) register_19 (.D(WriteData), .en(and_19_out), .clk(Clock), .Q(register_19_q), .clr(Reset));
  Register #(.width(32)) register_20 (.D(WriteData), .en(and_20_out), .clk(Clock), .Q(register_20_q), .clr(Reset));
  Register #(.width(32)) register_21 (.D(WriteData), .en(and_21_out), .clk(Clock), .Q(register_21_q), .clr(Reset));
  Register #(.width(32)) register_22 (.D(WriteData), .en(and_22_out), .clk(Clock), .Q(register_22_q), .clr(Reset));
  Register #(.width(32)) register_23 (.D(WriteData), .en(and_23_out), .clk(Clock), .Q(register_23_q), .clr(Reset));
  Register #(.width(32)) register_24 (.D(WriteData), .en(and_24_out), .clk(Clock), .Q(register_24_q), .clr(Reset));
  Register #(.width(32)) register_25 (.D(WriteData), .en(and_25_out), .clk(Clock), .Q(register_25_q), .clr(Reset));
  Register #(.width(32)) register_26 (.D(WriteData), .en(and_26_out), .clk(Clock), .Q(register_26_q), .clr(Reset));
  Register #(.width(32)) register_27 (.D(WriteData), .en(and_27_out), .clk(Clock), .Q(register_27_q), .clr(Reset));
  Register #(.width(32)) register_28 (.D(WriteData), .en(and_28_out), .clk(Clock), .Q(register_28_q), .clr(Reset));
  Register #(.width(32)) register_29 (.D(WriteData), .en(and_29_out), .clk(Clock), .Q(register_29_q), .clr(Reset));
  Register #(.width(32)) register_30 (.D(WriteData), .en(and_30_out), .clk(Clock), .Q(register_30_q), .clr(Reset));
  Register #(.width(32)) register_31 (.D(WriteData), .en(and_31_out), .clk(Clock), .Q(register_31_q), .clr(Reset));
  Register #(.width(32)) register_32 (.D(WriteData), .en(and_32_out), .clk(Clock), .Q(register_32_q), .clr(Reset));
  Multiplexer #(.select(5), .width(32)) multiplexer_1 (
    .in0(register_1_q), .in1(register_2_q), .in2(register_3_q), .in3(register_4_q), .in4(register_5_q),
    .in5(register_6_q), .in6(register_7_q), .in7(register_8_q), .in8(register_9_q), .in9(register_10_q),
    .in10(register_11_q), .in11(register_12_q), .in12(register_13_q), .in13(register_14_q),
    .in14(register_15_q), .in15(register_16_q), .in16(register_17_q), .in17(register_18_q),
    .in18(register_19_q), .in19(register_20_q), .in20(register_21_q), .in21(register_22_q),
    .in22(register_23_q), .in23(register_24_q), .in24(register_25_q), .in25(register_26_q),
    .in26(register_27_q), .in27(register_28_q), .in28(register_29_q), .in29(register_30_q),
    .in30(register_31_q), .in31(register_32_q), .out(ReadData1), .sel(ReadReg1));
  Multiplexer #(.select(5), .width(32)) multiplexer_2 (
    .in0(register_1_q), .in1(register_2_q), .in2(register_3_q), .in3(register_4_q), .in4(register_5_q),
    .in5(register_6_q), .in6(register_7_q), .in7(register_8_q), .in8(register_9_q), .in9(register_10_q),
    .in10(register_11_q), .in11(register_12_q), .in12(register_13_q), .in13(register_14_q),
    .in14(register_15_q), .in15(register_16_q), .in16(register_17_q), .in17(register_18_q),
    .in18(register_19_q), .in19(register_20_q), .in20(register_21_q), .in21(register_22_q),
    .in22(register_23_q), .in23(register_24_q), .in24(register_25_q), .in25(register_26_q),
    .in26(register_27_q), .in27(register_28_q), .in28(register_29_q), .in29(register_30_q),
    .in30(register_31_q), .in31(register_32_q), .out(ReadData2), .sel(ReadReg2));

  // Notes on the sheet:
  //   $0 is always 0
  //   For simplicity, $at ($1) is set to 0x1001000
endmodule

module one_bit_ALU (
  input  A,
  input  B,
  input  [1:0] selector,
  input  carry_in,
  input  A_invert,
  input  B_invert,
  output Q,
  output carry_out
);

  wire adder_1_out, and_1_out, multiplexer_1_out, multiplexer_2_out, not_1_out, not_2_out, or_1_out;

  not not_1 (not_1_out, A);
  not not_2 (not_2_out, B);
  Multiplexer multiplexer_1 (.in0(A), .in1(not_1_out), .out(multiplexer_1_out), .sel(A_invert));
  Multiplexer multiplexer_2 (.in0(B), .in1(not_2_out), .out(multiplexer_2_out), .sel(B_invert));
  and and_1 (and_1_out, multiplexer_1_out, multiplexer_2_out);
  or or_1 (or_1_out, multiplexer_1_out, multiplexer_2_out);
  Adder #(.width(1)) adder_1 (
    .a(multiplexer_1_out), .b(multiplexer_2_out), .out(adder_1_out), .cin(carry_in), .cout(carry_out));
  Multiplexer #(.select(2)) multiplexer_3 (
    .in0(and_1_out), .in1(or_1_out), .in2(adder_1_out), .out(Q), .sel(selector));  // open: in3
endmodule

module ALU_32_bits (
  input  [31:0] A,
  input  [31:0] B,
  input  [3:0] Operation,
  output [31:0] Q,
  output carry_out,
  output zero
);

  wire one_bit_alu_2_carry_out, one_bit_alu_3_carry_out, one_bit_alu_4_carry_out, one_bit_alu_5_carry_out,
       one_bit_alu_6_carry_out, one_bit_alu_7_carry_out, one_bit_alu_8_carry_out, one_bit_alu_9_carry_out,
       one_bit_alu_10_carry_out, one_bit_alu_11_carry_out, one_bit_alu_12_carry_out,
       one_bit_alu_13_carry_out, one_bit_alu_14_carry_out, one_bit_alu_15_carry_out,
       one_bit_alu_16_carry_out, one_bit_alu_17_carry_out, one_bit_alu_18_carry_out,
       one_bit_alu_19_carry_out, one_bit_alu_20_carry_out, one_bit_alu_21_carry_out,
       one_bit_alu_22_carry_out, one_bit_alu_23_carry_out, one_bit_alu_24_carry_out,
       one_bit_alu_25_carry_out, one_bit_alu_26_carry_out, one_bit_alu_27_carry_out,
       one_bit_alu_28_carry_out, one_bit_alu_29_carry_out, one_bit_alu_30_carry_out,
       one_bit_alu_31_carry_out, one_bit_alu_32_carry_out;

  one_bit_ALU one_bit_alu_1 (
    .A(A[31]), .B(B[31]), .selector(Operation[1:0]), .carry_in(one_bit_alu_2_carry_out),
    .A_invert(Operation[3]), .B_invert(Operation[2]), .Q(Q[31]), .carry_out(carry_out));
  one_bit_ALU one_bit_alu_2 (
    .A(A[30]), .B(B[30]), .selector(Operation[1:0]), .carry_in(one_bit_alu_3_carry_out),
    .A_invert(Operation[3]), .B_invert(Operation[2]), .Q(Q[30]), .carry_out(one_bit_alu_2_carry_out));
  one_bit_ALU one_bit_alu_3 (
    .A(A[29]), .B(B[29]), .selector(Operation[1:0]), .carry_in(one_bit_alu_4_carry_out),
    .A_invert(Operation[3]), .B_invert(Operation[2]), .Q(Q[29]), .carry_out(one_bit_alu_3_carry_out));
  one_bit_ALU one_bit_alu_4 (
    .A(A[28]), .B(B[28]), .selector(Operation[1:0]), .carry_in(one_bit_alu_5_carry_out),
    .A_invert(Operation[3]), .B_invert(Operation[2]), .Q(Q[28]), .carry_out(one_bit_alu_4_carry_out));
  one_bit_ALU one_bit_alu_5 (
    .A(A[27]), .B(B[27]), .selector(Operation[1:0]), .carry_in(one_bit_alu_6_carry_out),
    .A_invert(Operation[3]), .B_invert(Operation[2]), .Q(Q[27]), .carry_out(one_bit_alu_5_carry_out));
  one_bit_ALU one_bit_alu_6 (
    .A(A[26]), .B(B[26]), .selector(Operation[1:0]), .carry_in(one_bit_alu_7_carry_out),
    .A_invert(Operation[3]), .B_invert(Operation[2]), .Q(Q[26]), .carry_out(one_bit_alu_6_carry_out));
  one_bit_ALU one_bit_alu_7 (
    .A(A[25]), .B(B[25]), .selector(Operation[1:0]), .carry_in(one_bit_alu_8_carry_out),
    .A_invert(Operation[3]), .B_invert(Operation[2]), .Q(Q[25]), .carry_out(one_bit_alu_7_carry_out));
  one_bit_ALU one_bit_alu_8 (
    .A(A[24]), .B(B[24]), .selector(Operation[1:0]), .carry_in(one_bit_alu_9_carry_out),
    .A_invert(Operation[3]), .B_invert(Operation[2]), .Q(Q[24]), .carry_out(one_bit_alu_8_carry_out));
  one_bit_ALU one_bit_alu_9 (
    .A(A[23]), .B(B[23]), .selector(Operation[1:0]), .carry_in(one_bit_alu_10_carry_out),
    .A_invert(Operation[3]), .B_invert(Operation[2]), .Q(Q[23]), .carry_out(one_bit_alu_9_carry_out));
  one_bit_ALU one_bit_alu_10 (
    .A(A[22]), .B(B[22]), .selector(Operation[1:0]), .carry_in(one_bit_alu_11_carry_out),
    .A_invert(Operation[3]), .B_invert(Operation[2]), .Q(Q[22]), .carry_out(one_bit_alu_10_carry_out));
  one_bit_ALU one_bit_alu_11 (
    .A(A[21]), .B(B[21]), .selector(Operation[1:0]), .carry_in(one_bit_alu_12_carry_out),
    .A_invert(Operation[3]), .B_invert(Operation[2]), .Q(Q[21]), .carry_out(one_bit_alu_11_carry_out));
  one_bit_ALU one_bit_alu_12 (
    .A(A[20]), .B(B[20]), .selector(Operation[1:0]), .carry_in(one_bit_alu_13_carry_out),
    .A_invert(Operation[3]), .B_invert(Operation[2]), .Q(Q[20]), .carry_out(one_bit_alu_12_carry_out));
  one_bit_ALU one_bit_alu_13 (
    .A(A[19]), .B(B[19]), .selector(Operation[1:0]), .carry_in(one_bit_alu_14_carry_out),
    .A_invert(Operation[3]), .B_invert(Operation[2]), .Q(Q[19]), .carry_out(one_bit_alu_13_carry_out));
  one_bit_ALU one_bit_alu_14 (
    .A(A[18]), .B(B[18]), .selector(Operation[1:0]), .carry_in(one_bit_alu_15_carry_out),
    .A_invert(Operation[3]), .B_invert(Operation[2]), .Q(Q[18]), .carry_out(one_bit_alu_14_carry_out));
  one_bit_ALU one_bit_alu_15 (
    .A(A[17]), .B(B[17]), .selector(Operation[1:0]), .carry_in(one_bit_alu_16_carry_out),
    .A_invert(Operation[3]), .B_invert(Operation[2]), .Q(Q[17]), .carry_out(one_bit_alu_15_carry_out));
  one_bit_ALU one_bit_alu_16 (
    .A(A[16]), .B(B[16]), .selector(Operation[1:0]), .carry_in(one_bit_alu_17_carry_out),
    .A_invert(Operation[3]), .B_invert(Operation[2]), .Q(Q[16]), .carry_out(one_bit_alu_16_carry_out));
  one_bit_ALU one_bit_alu_17 (
    .A(A[15]), .B(B[15]), .selector(Operation[1:0]), .carry_in(one_bit_alu_18_carry_out),
    .A_invert(Operation[3]), .B_invert(Operation[2]), .Q(Q[15]), .carry_out(one_bit_alu_17_carry_out));
  one_bit_ALU one_bit_alu_18 (
    .A(A[14]), .B(B[14]), .selector(Operation[1:0]), .carry_in(one_bit_alu_19_carry_out),
    .A_invert(Operation[3]), .B_invert(Operation[2]), .Q(Q[14]), .carry_out(one_bit_alu_18_carry_out));
  one_bit_ALU one_bit_alu_19 (
    .A(A[13]), .B(B[13]), .selector(Operation[1:0]), .carry_in(one_bit_alu_20_carry_out),
    .A_invert(Operation[3]), .B_invert(Operation[2]), .Q(Q[13]), .carry_out(one_bit_alu_19_carry_out));
  one_bit_ALU one_bit_alu_20 (
    .A(A[12]), .B(B[12]), .selector(Operation[1:0]), .carry_in(one_bit_alu_21_carry_out),
    .A_invert(Operation[3]), .B_invert(Operation[2]), .Q(Q[12]), .carry_out(one_bit_alu_20_carry_out));
  one_bit_ALU one_bit_alu_21 (
    .A(A[11]), .B(B[11]), .selector(Operation[1:0]), .carry_in(one_bit_alu_22_carry_out),
    .A_invert(Operation[3]), .B_invert(Operation[2]), .Q(Q[11]), .carry_out(one_bit_alu_21_carry_out));
  one_bit_ALU one_bit_alu_22 (
    .A(A[10]), .B(B[10]), .selector(Operation[1:0]), .carry_in(one_bit_alu_23_carry_out),
    .A_invert(Operation[3]), .B_invert(Operation[2]), .Q(Q[10]), .carry_out(one_bit_alu_22_carry_out));
  one_bit_ALU one_bit_alu_23 (
    .A(A[9]), .B(B[9]), .selector(Operation[1:0]), .carry_in(one_bit_alu_24_carry_out),
    .A_invert(Operation[3]), .B_invert(Operation[2]), .Q(Q[9]), .carry_out(one_bit_alu_23_carry_out));
  one_bit_ALU one_bit_alu_24 (
    .A(A[8]), .B(B[8]), .selector(Operation[1:0]), .carry_in(one_bit_alu_25_carry_out),
    .A_invert(Operation[3]), .B_invert(Operation[2]), .Q(Q[8]), .carry_out(one_bit_alu_24_carry_out));
  one_bit_ALU one_bit_alu_25 (
    .A(A[7]), .B(B[7]), .selector(Operation[1:0]), .carry_in(one_bit_alu_26_carry_out),
    .A_invert(Operation[3]), .B_invert(Operation[2]), .Q(Q[7]), .carry_out(one_bit_alu_25_carry_out));
  one_bit_ALU one_bit_alu_26 (
    .A(A[6]), .B(B[6]), .selector(Operation[1:0]), .carry_in(one_bit_alu_27_carry_out),
    .A_invert(Operation[3]), .B_invert(Operation[2]), .Q(Q[6]), .carry_out(one_bit_alu_26_carry_out));
  one_bit_ALU one_bit_alu_27 (
    .A(A[5]), .B(B[5]), .selector(Operation[1:0]), .carry_in(one_bit_alu_28_carry_out),
    .A_invert(Operation[3]), .B_invert(Operation[2]), .Q(Q[5]), .carry_out(one_bit_alu_27_carry_out));
  one_bit_ALU one_bit_alu_28 (
    .A(A[4]), .B(B[4]), .selector(Operation[1:0]), .carry_in(one_bit_alu_29_carry_out),
    .A_invert(Operation[3]), .B_invert(Operation[2]), .Q(Q[4]), .carry_out(one_bit_alu_28_carry_out));
  one_bit_ALU one_bit_alu_29 (
    .A(A[3]), .B(B[3]), .selector(Operation[1:0]), .carry_in(one_bit_alu_30_carry_out),
    .A_invert(Operation[3]), .B_invert(Operation[2]), .Q(Q[3]), .carry_out(one_bit_alu_29_carry_out));
  one_bit_ALU one_bit_alu_30 (
    .A(A[2]), .B(B[2]), .selector(Operation[1:0]), .carry_in(one_bit_alu_31_carry_out),
    .A_invert(Operation[3]), .B_invert(Operation[2]), .Q(Q[2]), .carry_out(one_bit_alu_30_carry_out));
  one_bit_ALU one_bit_alu_31 (
    .A(A[1]), .B(B[1]), .selector(Operation[1:0]), .carry_in(one_bit_alu_32_carry_out),
    .A_invert(Operation[3]), .B_invert(Operation[2]), .Q(Q[1]), .carry_out(one_bit_alu_31_carry_out));
  one_bit_ALU one_bit_alu_32 (
    .A(A[0]), .B(B[0]), .selector(Operation[1:0]), .carry_in(Operation[2]), .A_invert(Operation[3]),
    .B_invert(Operation[2]), .Q(Q[0]), .carry_out(one_bit_alu_32_carry_out));
  nor nor_1 (zero, Q[31], Q[30], Q[29], Q[28], Q[27], Q[26], Q[25], Q[24], Q[23], Q[22], Q[21], Q[20], Q[19], Q[18], Q[17], Q[16], Q[15], Q[14], Q[13], Q[12], Q[11], Q[10], Q[9], Q[8], Q[7], Q[6], Q[5], Q[4], Q[3], Q[2], Q[1], Q[0]);

  // Notes on the sheet:
  //   (Select)
  //   (Ainvert)
  //   (Bnegate)
  //   (Binvert)
  //   (Carry_in)
endmodule

module MemoryConverter (
  input  [31:0] in_1,
  output [7:0] out_2
);

  wire [7:0] bit_extender_1_out;

  Bit_Extender #(.in_width(32), .out_width(8), .\type ("zero")) bit_extender_1 (.in(in_1), .out(bit_extender_1_out));
  Divider divider_1 (.a(bit_extender_1_out), .b(8'h4), .out(out_2));  // open: upper, rem
endmodule

module PC (
  input  [31:0] PC_in,
  input  Clock,
  input  Reset,
  output [31:0] PC_out
);

  wire buffer_1_out, buffer_2_out, buffer_3_out, multiplexer_2_out;
  wire [31:0] multiplexer_1_out;

  Multiplexer #(.width(32)) multiplexer_1 (.in0(PC_in), .in1(32'h400000), .out(multiplexer_1_out), .sel(Reset));
  buf buffer_1 (buffer_1_out, Reset);
  buf buffer_2 (buffer_2_out, buffer_1_out);
  Register #(.width(32)) register_1 (.D(multiplexer_1_out), .clk(multiplexer_2_out), .Q(PC_out));  // open: en, clr
  Multiplexer multiplexer_2 (.in0(Clock), .in1(buffer_3_out), .out(multiplexer_2_out), .sel(Reset));
  buf buffer_3 (buffer_3_out, buffer_2_out);

  // Notes on the sheet:
  //   There's probably a better way to handle the reset, but this works
  //   (the buffers are there to make sure that the clock input
  //   reaches the register *after* 0x00400000 has reached the data input)
endmodule
